// Logisim project Part1.circ as structural Verilog: 1 circuit, main circuit main
module main (
  input  [3:0] FunSel,
  input  A0,
  input  A1,
  input  A2,
  input  A3,
  input  A4,
  input  A5,
  input  A6,
  input  A7,
  input  B0,
  input  B1,
  input  B2,
  input  B3,
  input  B4,
  input  B5,
  input  B6,
  input  B7,
  output ZERO,
  output CARRY,
  output NEGATIVE,
  output OVERFLOW,
  output OutALU0,
  output OutALU1,
  output OutALU2,
  output OutALU3,
  output OutALU4,
  output OutALU5,
  output OutALU6,
  output OutALU7
);

  wire main_1_p15, main_1_p16, main_1_p17, main_1_p18, main_1_p19, main_1_p20, main_1_p21, main_1_p22,
       main_1_p23, main_2_p17, main_2_p18, main_2_p19, main_2_p20, main_2_p21, main_2_p22, main_2_p23,
       main_2_p24, main_2_p25, main_2_p26, main_2_p27, main_2_p28, main_2_p29, main_2_p30, main_2_p31,
       main_2_p32, main_2_p33, main_2_p34, main_2_p35, main_2_p36, main_2_p37, main_2_p38, main_2_p39,
       main_2_p40, main_2_p41, main_2_p42, main_2_p43, main_2_p44, main_2_p45, main_2_p46, main_2_p47,
       main_3_p18, main_3_p19, main_3_p20, main_3_p21, main_3_p22, main_3_p23, main_3_p24, main_3_p25,
       main_3_p26, main_3_p27, main_3_p28, main_3_p29, main_3_p30, main_3_p31, main_3_p32, main_3_p33,
       main_3_p34, main_3_p35, main_3_p36, main_3_p37, main_3_p38, main_3_p39, main_3_p40, main_3_p41,
       main_3_p42, main_3_p43, main_3_p44, main_3_p45, main_3_p46, main_3_p47, main_3_p48, main_3_p49,
       main_3_p50, main_3_p51;
  wire [3:0] adder_2_out, multiplexer_1_out, multiplexer_2_out, multiplexer_3_out, multiplexer_4_out,
       multiplexer_13_out, multiplexer_14_out;
  wire [7:0] adder_1_out, adder_3_out, not_1_out, not_2_out, not_3_out;
  wire [7:4] adder_2_out_2;

  assign not_1_out = ~{A7, A6, A5, A4, A3, A2, A1, A0};  // NOT_Gate not_1, 8 bits wide
  Hex_Digit_Display hex_digit_display_1 (.value({3'b000, A7}));  // open: dp
  Hex_Digit_Display hex_digit_display_2 (.value({3'b000, B7}));  // open: dp
  Adder adder_1 (.a(not_1_out), .b(8'h1), .out(adder_1_out));  // open: cin, cout
  Hex_Digit_Display hex_digit_display_3 (.value(multiplexer_2_out));  // open: dp
  Hex_Digit_Display hex_digit_display_4 (.value(multiplexer_4_out));  // open: dp
  assign not_2_out = ~{B7, B6, B5, B4, B3, B2, B1, B0};  // NOT_Gate not_2, 8 bits wide
  Hex_Digit_Display hex_digit_display_5 (.value(multiplexer_1_out));  // open: dp
  Hex_Digit_Display hex_digit_display_6 (.value(multiplexer_3_out));  // open: dp
  Adder adder_2 (.a(not_2_out), .b(8'h1), .out({adder_2_out_2, adder_2_out}));  // open: cin, cout
  Multiplexer #(.width(4), .enable("false")) multiplexer_1 (
    .in0({A3, A2, A1, A0}), .in1(adder_1_out[3:0]), .out(multiplexer_1_out), .sel(A7));
  Multiplexer #(.width(4), .enable("false")) multiplexer_2 (
    .in0({A7, A6, A5, A4}), .in1(adder_1_out[7:4]), .out(multiplexer_2_out), .sel(A7));
  Multiplexer #(.width(4), .enable("false")) multiplexer_3 (
    .in0({B3, B2, B1, B0}), .in1(adder_2_out), .out(multiplexer_3_out), .sel(B7));
  Multiplexer #(.width(4), .enable("false")) multiplexer_4 (
    .in0({B7, B6, B5, B4}), .in1(adder_2_out_2), .out(multiplexer_4_out), .sel(B7));
  // Arithmetic_Unit_main main_1: pin names not known; wires that end beside it: FunSel[1], FunSel[0], CARRY, A0, B0, A1, B1, A2, B2, A3, B3, A4, B4, A5, main_1_p15, main_1_p16, main_1_p17, main_1_p18, main_1_p19, main_1_p20, main_1_p21, main_1_p22, main_1_p23
  // Logic_Unit_main main_2: pin names not known; wires that end beside it: B5, A6, B6, A7, B7, A0, B0, A1, B1, A2, B2, A3, B3, A4, B4, A5, main_2_p17, main_2_p18, main_2_p19, main_2_p20, main_2_p21, main_2_p22, main_2_p23, main_2_p24, main_2_p25, main_2_p26, main_2_p27, main_2_p28, main_2_p29, main_2_p30, main_2_p31, main_2_p32, main_2_p33, main_2_p34, main_2_p35, main_2_p36, main_2_p37, main_2_p38, main_2_p39, main_2_p40, main_2_p41, main_2_p42, main_2_p43, main_2_p44, main_2_p45, main_2_p46, main_2_p47
  // Shifting_Unit_main main_3: pin names not known; wires that end beside it: B5, A6, B6, A7, B7, FunSel[2], FunSel[1], FunSel[0], CARRY, A0, A1, A2, A3, A4, A5, A6, A7, main_3_p18, main_3_p19, main_3_p20, main_3_p21, main_3_p22, main_3_p23, main_3_p24, main_3_p25, main_3_p26, main_3_p27, main_3_p28, main_3_p29, main_3_p30, main_3_p31, main_3_p32, main_3_p33, main_3_p34, main_3_p35, main_3_p36, main_3_p37, main_3_p38, main_3_p39, main_3_p40, main_3_p41, main_3_p42, main_3_p43, main_3_p44, main_3_p45, main_3_p46, main_3_p47, main_3_p48, main_3_p49, main_3_p50, main_3_p51
  assign not_3_out = ~{OutALU7, OutALU6, OutALU5, OutALU4, OutALU3, OutALU2, OutALU1, OutALU0};  // NOT_Gate not_3, 8 bits wide
  Adder adder_3 (.a(not_3_out), .b(8'h1), .out(adder_3_out));  // open: cin, cout
  Multiplexer #(.select(4), .enable("false")) multiplexer_5 (
    .in0(main_2_p17), .in1(main_2_p18), .in2(main_2_p19), .in3(main_2_p20), .in4(main_1_p15),
    .in5(main_1_p15), .in6(main_1_p15), .in7(main_2_p21), .in8(main_2_p22), .in9(main_2_p23),
    .in10(main_3_p43), .in11(main_3_p43), .in12(main_3_p43), .in13(main_3_p43), .in14(main_3_p43),
    .in15(main_3_p43), .out(OutALU0), .sel(FunSel));
  Multiplexer #(.select(4), .enable("false")) multiplexer_6 (
    .in0(main_2_p24), .in1(main_2_p25), .in2(main_2_p26), .in3(main_2_p27), .in4(main_1_p16),
    .in5(main_1_p16), .in6(main_1_p16), .in7(main_2_p28), .in8(main_2_p29), .in9(main_2_p30),
    .in10(main_3_p44), .in11(main_3_p44), .in12(main_3_p44), .in13(main_3_p44), .in14(main_3_p44),
    .in15(main_3_p44), .out(OutALU1), .sel(FunSel));
  Multiplexer #(.select(4), .enable("false")) multiplexer_7 (
    .in0(main_2_p31), .in1(main_2_p32), .in2(main_2_p33), .in3(main_2_p34), .in4(main_1_p17),
    .in5(main_1_p17), .in6(main_1_p17), .in7(main_2_p35), .in8(main_2_p36), .in9(main_2_p37),
    .in10(main_3_p45), .in11(main_3_p45), .in12(main_3_p45), .in13(main_3_p45), .in14(main_3_p45),
    .in15(main_3_p45), .out(OutALU2), .sel(FunSel));
  Multiplexer #(.select(4), .enable("false")) multiplexer_8 (
    .in0(main_2_p38), .in1(main_2_p39), .in2(main_2_p40), .in3(main_2_p41), .in4(main_1_p18),
    .in5(main_1_p18), .in6(main_1_p18), .in7(main_2_p42), .in8(main_2_p43), .in9(main_2_p44),
    .in10(main_3_p46), .in11(main_3_p46), .in12(main_3_p46), .in13(main_3_p46), .in14(main_3_p46),
    .in15(main_3_p46), .out(OutALU3), .sel(FunSel));
  Multiplexer #(.select(4), .enable("false")) multiplexer_9 (
    .in0(main_2_p45), .in1(main_2_p46), .in2(main_2_p47), .in3(main_3_p18), .in4(main_1_p19),
    .in5(main_1_p19), .in6(main_1_p19), .in7(main_3_p19), .in8(main_3_p20), .in9(main_3_p21),
    .in10(main_3_p47), .in11(main_3_p47), .in12(main_3_p47), .in13(main_3_p47), .in14(main_3_p47),
    .in15(main_3_p47), .out(OutALU4), .sel(FunSel));
  Multiplexer #(.select(4), .enable("false")) multiplexer_10 (
    .in0(main_3_p22), .in1(main_3_p23), .in2(main_3_p24), .in3(main_3_p25), .in4(main_1_p20),
    .in5(main_1_p20), .in6(main_1_p20), .in7(main_3_p26), .in8(main_3_p27), .in9(main_3_p28),
    .in10(main_3_p48), .in11(main_3_p48), .in12(main_3_p48), .in13(main_3_p48), .in14(main_3_p48),
    .in15(main_3_p48), .out(OutALU5), .sel(FunSel));
  Multiplexer #(.select(4), .enable("false")) multiplexer_11 (
    .in0(main_3_p29), .in1(main_3_p30), .in2(main_3_p31), .in3(main_3_p32), .in4(main_1_p21),
    .in5(main_1_p21), .in6(main_1_p21), .in7(main_3_p33), .in8(main_3_p34), .in9(main_3_p35),
    .in10(main_3_p49), .in11(main_3_p49), .in12(main_3_p49), .in13(main_3_p49), .in14(main_3_p49),
    .in15(main_3_p49), .out(OutALU6), .sel(FunSel));
  Multiplexer #(.select(4), .enable("false")) multiplexer_12 (
    .in0(main_3_p36), .in1(main_3_p37), .in2(main_3_p38), .in3(main_3_p39), .in4(main_1_p22),
    .in5(main_1_p22), .in6(main_1_p22), .in7(main_3_p40), .in8(main_3_p41), .in9(main_3_p42),
    .in10(main_3_p50), .in11(main_3_p50), .in12(main_3_p50), .in13(main_3_p50), .in14(main_3_p50),
    .in15(main_3_p50), .out(OutALU7), .sel(FunSel));
  Multiplexer #(.width(4), .enable("false")) multiplexer_13 (
    .in0({OutALU3, OutALU2, OutALU1, OutALU0}), .in1(adder_3_out[3:0]), .out(multiplexer_13_out),
    .sel(OutALU7));
  Multiplexer #(.width(4), .enable("false")) multiplexer_14 (
    .in0({OutALU7, OutALU6, OutALU5, OutALU4}), .in1(adder_3_out[7:4]), .out(multiplexer_14_out),
    .sel(OutALU7));
  Hex_Digit_Display hex_digit_display_7 (.value({3'b000, OutALU7}));  // open: dp
  Hex_Digit_Display hex_digit_display_8 (.value(multiplexer_14_out));  // open: dp
  Hex_Digit_Display hex_digit_display_9 (.value(multiplexer_13_out));  // open: dp
  // ZCNO_Register_main main_4: pin names not known; wires that end beside it: FunSel, OutALU0, OutALU1, OutALU2, OutALU3, OutALU4, OutALU5, OutALU6, OutALU7, main_1_p23, main_3_p51, A6, A7, B7, ZERO, CARRY, NEGATIVE, OVERFLOW

  // Notes on the sheet:
  //   Sign of A
  //   Sign of B
  //   Logic Unit
  //   Shifting Unit
  //   Arithmetic Unit
  //   Sign of OutALU
  //   ZCNO Register
endmodule
