// Logisim project Part2a_final.circ as structural Verilog: 1 circuit, main circuit main
module main (
  input  [1:0] OutASel,
  input  [1:0] OutBSel,
  input  [1:0] FunSel,
  input  [3:0] RegSel,
  input  I0,
  input  I1,
  input  I2,
  input  I3,
  input  I4,
  input  I5,
  input  I6,
  input  I7,
  output [7:0] R0,
  output [7:0] R2,
  output [7:0] R1,
  output [7:0] R3,
  output OutA0,
  output OutB0,
  output OutA1,
  output OutB1,
  output OutA2,
  output OutB2,
  output OutA3,
  output OutB3,
  output OutA4,
  output OutB4,
  output OutA5,
  output OutB5,
  output OutA6,
  output OutB6,
  output OutA7,
  output OutB7
);

  Hex_Digit_Display hex_digit_display_1 (.value({I7, I6, I5, I4}));  // open: dp
  Hex_Digit_Display hex_digit_display_2 (.value({I3, I2, I1, I0}));  // open: dp
  // _8bit_register_final_main R0: pin names not known; wires that end beside it: FunSel, RegSel[0], I0, I1, I2, I3, I4, I5, I6, I7, R0[0], R0[1], R0[2], R0[3], R0[4], R0[5], R0[6], R0[7]
  // _8bit_register_final_main R1: pin names not known; wires that end beside it: FunSel, RegSel[1], I0, I1, I2, I3, I4, I5, I6, I7, R1[0], R1[1], R1[2], R1[3], R1[4], R1[5], R1[6], R1[7]
  // _8bit_register_final_main R2: pin names not known; wires that end beside it: FunSel, RegSel[2], I0, I1, I2, I3, I4, I5, I6, I7, R2[0], R2[1], R2[2], R2[3], R2[4], R2[5], R2[6], R2[7]
  // _8bit_register_final_main R3: pin names not known; wires that end beside it: FunSel, RegSel[3], I0, I1, I2, I3, I4, I5, I6, I7, R3[0], R3[1], R3[2], R3[3], R3[4], R3[5], R3[6], R3[7]
  Multiplexer #(.select(2)) multiplexer_1 (
    .in0(R0[0]), .in1(R1[0]), .in2(R2[0]), .in3(R3[0]), .out(OutA0), .sel(OutASel));  // open: en
  Multiplexer #(.select(2)) multiplexer_2 (
    .in0(R0[1]), .in1(R1[1]), .in2(R2[1]), .in3(R3[1]), .out(OutA1), .sel(OutASel));  // open: en
  Multiplexer #(.select(2)) multiplexer_3 (
    .in0(R0[2]), .in1(R1[2]), .in2(R2[2]), .in3(R3[2]), .out(OutA2), .sel(OutASel));  // open: en
  Multiplexer #(.select(2)) multiplexer_4 (
    .in0(R0[3]), .in1(R1[3]), .in2(R2[3]), .in3(R3[3]), .out(OutA3), .sel(OutASel));  // open: en
  Multiplexer #(.select(2)) multiplexer_5 (
    .in0(R0[4]), .in1(R1[4]), .in2(R2[4]), .in3(R3[4]), .out(OutA4), .sel(OutASel));  // open: en
  Multiplexer #(.select(2)) multiplexer_6 (
    .in0(R0[5]), .in1(R1[5]), .in2(R2[5]), .in3(R3[5]), .out(OutA5), .sel(OutASel));  // open: en
  Multiplexer #(.select(2)) multiplexer_7 (
    .in0(R0[6]), .in1(R1[6]), .in2(R2[6]), .in3(R3[6]), .out(OutA6), .sel(OutASel));  // open: en
  Multiplexer #(.select(2)) multiplexer_8 (
    .in0(R0[7]), .in1(R1[7]), .in2(R2[7]), .in3(R3[7]), .out(OutA7), .sel(OutASel));  // open: en
  Multiplexer #(.select(2)) multiplexer_9 (
    .in0(R0[0]), .in1(R1[0]), .in2(R2[0]), .in3(R3[0]), .out(OutB0), .sel(OutBSel));  // open: en
  Multiplexer #(.select(2)) multiplexer_10 (
    .in0(R0[1]), .in1(R1[1]), .in2(R2[1]), .in3(R3[1]), .out(OutB1), .sel(OutBSel));  // open: en
  Multiplexer #(.select(2)) multiplexer_11 (
    .in0(R0[2]), .in1(R1[2]), .in2(R2[2]), .in3(R3[2]), .out(OutB2), .sel(OutBSel));  // open: en
  Multiplexer #(.select(2)) multiplexer_12 (
    .in0(R0[3]), .in1(R1[3]), .in2(R2[3]), .in3(R3[3]), .out(OutB3), .sel(OutBSel));  // open: en
  Multiplexer #(.select(2)) multiplexer_13 (
    .in0(R0[4]), .in1(R1[4]), .in2(R2[4]), .in3(R3[4]), .out(OutB4), .sel(OutBSel));  // open: en
  Multiplexer #(.select(2)) multiplexer_14 (
    .in0(R0[5]), .in1(R1[5]), .in2(R2[5]), .in3(R3[5]), .out(OutB5), .sel(OutBSel));  // open: en
  Multiplexer #(.select(2)) multiplexer_15 (
    .in0(R0[6]), .in1(R1[6]), .in2(R2[6]), .in3(R3[6]), .out(OutB6), .sel(OutBSel));  // open: en
  Multiplexer #(.select(2)) multiplexer_16 (
    .in0(R0[7]), .in1(R1[7]), .in2(R2[7]), .in3(R3[7]), .out(OutB7), .sel(OutBSel));  // open: en
  Hex_Digit_Display hex_digit_display_3 (.value({OutA7, OutA6, OutA5, OutA4}));  // open: dp
  Hex_Digit_Display hex_digit_display_4 (.value({OutB7, OutB6, OutB5, OutB4}));  // open: dp
  Hex_Digit_Display hex_digit_display_5 (.value({OutA3, OutA2, OutA1, OutA0}));  // open: dp
  Hex_Digit_Display hex_digit_display_6 (.value({OutB3, OutB2, OutB1, OutB0}));  // open: dp

  // Other names for the same wires on the sheet: R0_0 = R0[0]; R0_1 = R0[1]; R0_2 = R0[2]; R0_3 = R0[3]; R0_4 = R0[4];
  //   R0_5 = R0[5]; R0_6 = R0[6]; R0_7 = R0[7]; R1_0 = R1[0]; R1_1 = R1[1]; R1_2 = R1[2]; R1_3 = R1[3]; R1_4 = R1[4];
  //   R1_5 = R1[5]; R1_6 = R1[6]; R1_7 = R1[7]; R2_0 = R2[0]; R2_1 = R2[1]; R2_2 = R2[2]; R2_3 = R2[3]; R2_4 = R2[4];
  //   R2_5 = R2[5]; R2_6 = R2[6]; R2_7 = R2[7]; R3_0 = R3[0]; R3_1 = R3[1]; R3_2 = R3[2]; R3_3 = R3[3]; R3_4 = R3[4];
  //   R3_5 = R3[5]; R3_6 = R3[6]; R3_7 = R3[7]

  // Notes on the sheet:
  //   OutA
  //   OutB
endmodule
