// Logisim project Part2b_final.circ as structural Verilog: 1 circuit, main circuit main
module main (
  input  [1:0] OutCSel,
  input  [1:0] OutDSel,
  input  [1:0] FunSel,
  input  [2:0] RegSel,
  input  I0,
  input  I1,
  input  I2,
  input  I3,
  input  I4,
  input  I5,
  input  I6,
  input  I7,
  output [7:0] PC,
  output [7:0] SP,
  output [7:0] AR,
  output OutC0,
  output OutD0,
  output OutC1,
  output OutD1,
  output OutC2,
  output OutB2,
  output OutC3,
  output OutD3,
  output OutC4,
  output OutD4,
  output OutC5,
  output OutD5,
  output OutC6,
  output OutD6,
  output OutC7,
  output OutD7
);

  Hex_Digit_Display hex_digit_display_1 (.value({I7, I6, I5, I4}));  // open: dp
  Hex_Digit_Display hex_digit_display_2 (.value({{2{I2}}, I1, I0}));  // open: dp
  // _8bit_register_final_main PC: pin names not known; wires that end beside it: FunSel, RegSel[0], I0, I1, I2, I3, I4, I5, I6, I7, PC[0], PC[1], PC[2], PC[3], PC[4], PC[5], PC[6], PC[7]
  // _8bit_register_final_main AR: pin names not known; wires that end beside it: FunSel, RegSel[1], I0, I1, I2, I3, I4, I5, I6, I7, AR[0], AR[1], AR[2], AR[3], AR[4], AR[5], AR[6], AR[7]
  // _8bit_register_final_main SP: pin names not known; wires that end beside it: FunSel, RegSel[2], I0, I1, I2, I3, I4, I5, I6, I7, SP[0], SP[1], SP[2], SP[3], SP[4], SP[5], SP[6], SP[7]
  Multiplexer #(.select(2)) multiplexer_1 (
    .in0(PC[0]), .in1(AR[0]), .in2(SP[0]), .in3(PC[0]), .out(OutC0), .sel(OutCSel));  // open: en
  Multiplexer #(.select(2)) multiplexer_2 (
    .in0(PC[1]), .in1(AR[1]), .in2(SP[1]), .in3(PC[1]), .out(OutC1), .sel(OutCSel));  // open: en
  Multiplexer #(.select(2)) multiplexer_3 (
    .in0(PC[2]), .in1(AR[2]), .in2(SP[2]), .in3(PC[2]), .out(OutC2), .sel(OutCSel));  // open: en
  Multiplexer #(.select(2)) multiplexer_4 (
    .in0(PC[3]), .in1(AR[3]), .in2(SP[3]), .in3(PC[3]), .out(OutC3), .sel(OutCSel));  // open: en
  Multiplexer #(.select(2)) multiplexer_5 (
    .in0(PC[4]), .in1(AR[4]), .in2(SP[4]), .in3(PC[4]), .out(OutC4), .sel(OutCSel));  // open: en
  Multiplexer #(.select(2)) multiplexer_6 (
    .in0(PC[5]), .in1(AR[5]), .in2(SP[5]), .in3(PC[5]), .out(OutC5), .sel(OutCSel));  // open: en
  Multiplexer #(.select(2)) multiplexer_7 (
    .in0(PC[6]), .in1(AR[6]), .in2(SP[6]), .in3(PC[6]), .out(OutC6), .sel(OutCSel));  // open: en
  Multiplexer #(.select(2)) multiplexer_8 (
    .in0(PC[7]), .in1(AR[7]), .in2(SP[7]), .in3(PC[7]), .out(OutC7), .sel(OutCSel));  // open: en
  Multiplexer #(.select(2)) multiplexer_9 (
    .in0(PC[0]), .in1(AR[0]), .in2(SP[0]), .in3(PC[0]), .out(OutD0), .sel(OutDSel));  // open: en
  Multiplexer #(.select(2)) multiplexer_10 (
    .in0(PC[1]), .in1(AR[1]), .in2(SP[1]), .in3(PC[1]), .out(OutD1), .sel(OutDSel));  // open: en
  Multiplexer #(.select(2)) multiplexer_11 (
    .in0(PC[2]), .in1(AR[2]), .in2(SP[2]), .in3(PC[2]), .out(OutB2), .sel(OutDSel));  // open: en
  Multiplexer #(.select(2)) multiplexer_12 (
    .in0(PC[3]), .in1(AR[3]), .in2(SP[3]), .in3(PC[3]), .out(OutD3), .sel(OutDSel));  // open: en
  Multiplexer #(.select(2)) multiplexer_13 (
    .in0(PC[4]), .in1(AR[4]), .in2(SP[4]), .in3(PC[4]), .out(OutD4), .sel(OutDSel));  // open: en
  Multiplexer #(.select(2)) multiplexer_14 (
    .in0(PC[5]), .in1(AR[5]), .in2(SP[5]), .in3(PC[5]), .out(OutD5), .sel(OutDSel));  // open: en
  Multiplexer #(.select(2)) multiplexer_15 (
    .in0(PC[6]), .in1(AR[6]), .in2(SP[6]), .in3(PC[6]), .out(OutD6), .sel(OutDSel));  // open: en
  Multiplexer #(.select(2)) multiplexer_16 (
    .in0(PC[7]), .in1(AR[7]), .in2(SP[7]), .in3(PC[7]), .out(OutD7), .sel(OutDSel));  // open: en
  Hex_Digit_Display hex_digit_display_3 (.value({OutC7, OutC6, OutC5, OutC4}));  // open: dp
  Hex_Digit_Display hex_digit_display_4 (.value({OutD7, OutD6, OutD5, OutD4}));  // open: dp
  Hex_Digit_Display hex_digit_display_5 (.value({OutC3, OutC2, OutC1, OutC0}));  // open: dp
  Hex_Digit_Display hex_digit_display_6 (.value({OutD3, OutB2, OutD1, OutD0}));  // open: dp

  // Other names for the same wires on the sheet: AR_0 = AR[0]; AR_1 = AR[1]; AR_2 = AR[2]; AR_3 = AR[3]; AR_4 = AR[4];
  //   AR_5 = AR[5]; AR_6 = AR[6]; AR_7 = AR[7]; PC_0 = PC[0]; PC_1 = PC[1]; PC_2 = PC[2]; PC_3 = PC[3]; PC_4 = PC[4];
  //   PC_5 = PC[5]; PC_6 = PC[6]; PC_7 = PC[7]; SP_0 = SP[0]; SP_1 = SP[1]; SP_2 = SP[2]; SP_3 = SP[3]; SP_4 = SP[4];
  //   SP_5 = SP[5]; SP_6 = SP[6]; SP_7 = SP[7]

  // Notes on the sheet:
  //   OutC
  //   OutD
endmodule
