// Logisim project main.circ as structural Verilog: 1 circuit, main circuit main
module main (
  input  CLR,
  output [4:0] Opcode,
  output [7:0] R0,
  output [7:0] R1,
  output [2:0] DESTREG,
  output [7:0] R2,
  output [7:0] R3,
  output [3:0] FunSelALU,
  output [7:0] OutB,
  output ZERO,
  output CARRY,
  output NEGATIVE,
  output OVERFLOW,
  output [7:0] OutA,
  output [7:0] MUX_C_Out,
  output [4:0] out_16,
  output [3:0] RegSelRegister,
  output [1:0] FunSelRegister,
  output [1:0] OutBSel,
  output [1:0] OutASel,
  output [2:0] out_21,
  output [2:0] out_22,
  output [7:0] OutALU,
  output [2:0] SRCREG1,
  output [1:0] Rx,
  output [7:0] PC,
  output [15:0] D__load,
  output [7:0] AR,
  output [7:0] MuxA_Out,
  output [1:0] MuxASel,
  output [7:0] SP,
  output [2:0] out_32,
  output [7:0] OutC,
  output A,
  output [1:0] MuxBSel,
  output [2:0] SRCREG2,
  output [7:0] IR_7_0,
  output [2:0] RegSel,
  output [7:0] OutD,
  output [7:0] MUX_B_Out,
  output [1:0] FunSel,
  output [7:0] IR_15_8,
  output [1:0] OutCSel,
  output [4:0] Opcode_2,
  output out_45,
  output [1:0] OutDSel,
  output [1:0] RegSel_2,
  output [2:0] out_48,
  output [2:0] out_49,
  output [1:0] out_50,
  output [12:0] out_51,
  output [1:0] out_52,
  output [12:0] out_53,
  output [12:0] out_54,
  output [12:0] out_55,
  output [30:0] out_56,
  output [2:0] F4,
  output [1:0] CD,
  output [1:0] BR,
  output [2:0] F3,
  output [7:0] IR_7_0_2,
  output [7:0] IR_15_8_2,
  output [2:0] F2,
  output [3:0] FunSelALU_2,
  output [4:0] Opcode_3,
  output [4:0] F1,
  output [1:0] MuxASel_2,
  output [1:0] FunSelAddress,
  output [1:0] MuxBSel_2,
  output [2:0] RegSelAddress,
  output MuxCSel,
  output [1:0] OutCSel_2,
  output MuxDSel,
  output [1:0] OutDSel_2,
  output [3:0] RegSelRegister_2,
  output Str,
  output [15:0] out_77,
  output [1:0] FunSelRegister_2,
  output Sel,
  output LD,
  output [1:0] OutASel_2,
  output CLK,
  output [1:0] OutASel_3,
  output L_prime_H,
  output Enable
);

  wire and_1_out, and_2_out, and_3_out, and_4_out, and_5_out, and_6_out, and_7_out, and_8_out, and_9_out,
       and_10_out, and_11_out, and_12_out, and_13_out, and_14_out, and_15_out, and_16_out, and_17_out,
       and_18_out, and_19_out, and_20_out, and_21_out, and_22_out, and_23_out, and_24_out, and_25_out,
       and_26_out, and_27_out, and_28_out, and_29_out, and_30_out, and_31_out, and_32_out, and_33_out,
       and_34_out, and_35_out, and_36_out, and_37_out, and_38_out, and_39_out, and_40_out, and_41_out,
       CLK_2_out, CLK_out, clock_1_out, comparator_1_eq, comparator_1_lt, D0, D1, D2, D3, D4, D5, D6, D7, D8,
       D9, D10, D11, D12, D13, D14, D15, D16, D17, D18, F2_0, F2_1, F2_2, F2_3, F2_4, F2_5, F2_6, F2_7, F3_0,
       F3_1, F3_2, F3_3, F3_4, F3_5, F3_6, F3_7, F4_0, F4_1, F4_2, F4_3, F4_4, F4_5, F4_6, F4_7, nor_1_out,
       nor_2_out, nor_3_out, nor_4_out, nor_5_out, nor_6_out, nor_7_out, nor_8_out, nor_9_out, not_1_out,
       not_2_out, not_3_out, not_5_out, not_6_out, not_7_out, not_8_out, not_9_out, not_10_out, not_11_out,
       not_12_out, not_13_out, not_14_out, not_15_out, not_16_out, not_17_out, not_18_out, not_19_out,
       not_20_out, not_21_out, not_22_out, not_23_out, not_24_out, not_25_out, not_26_out, not_27_out,
       not_28_out, not_29_out, not_30_out, not_31_out, O0, O1, O2, O3, O4, O5, O6, O7, O8, O9, O10, O11, O12,
       O13, O14, O15, O16, O17, O18, O19, or_1_out, or_2_out, or_3_out, or_4_out, or_5_out, or_6_out,
       or_7_out, or_8_out, or_9_out, or_10_out, or_11_out, or_12_out, or_13_out, or_14_out, or_15_out,
       or_16_out, or_17_out, or_18_out, or_19_out, or_20_out, or_21_out, or_22_out, or_23_out, or_24_out,
       or_25_out, or_26_out, or_27_out, or_28_out, or_29_out, or_30_out, or_31_out, or_32_out, or_33_out, S;
  wire [0:0] multiplexer_10_out, not_4_out;
  wire [2:0] multiplexer_7_out, multiplexer_8_out, multiplexer_9_out, SRCREG1_m, SRCREG2_m;
  wire [7:0] main_2_p4;
  wire [12:0] CAR_q;

  D_Flip_Flop d_ff_1 (.clk(CLK_out), .D(DESTREG[0]), .Q(A), .en(1'b1));  // open: Qn, preset, reset
  Part2a_final_main main_1 (
    .OutASel(OutASel), .OutBSel(out_50), .FunSel(FunSelRegister), .RegSel(RegSelRegister), .I0(MuxA_Out[0]),
    .I1(MuxA_Out[1]), .I2(MuxA_Out[2]), .I3(MuxA_Out[3]), .I4(MuxA_Out[4]), .I5(MuxA_Out[5]),
    .I6(MuxA_Out[6]), .I7(MuxA_Out[7]), .R0(R0), .R1(R1), .R2(R2), .R3(R3), .OutA0(OutA[0]), .OutB0(OutB[0]),
    .OutA1(OutA[1]), .OutB1(OutB[1]), .OutA2(OutA[2]), .OutB2(OutB[2]), .OutA3(OutA[3]), .OutB3(OutB[3]),
    .OutA4(OutA[4]), .OutB4(OutB[4]), .OutA5(OutA[5]), .OutB5(OutB[5]), .OutA6(OutA[6]), .OutB6(OutB[6]),
    .OutA7(OutA[7]), .OutB7(OutB[7]));
  Multiplexer #(.select(2), .width(8), .enable("false")) multiplexer_1 (
    .in0(IR_7_0), .in1(main_2_p4), .in2(OutC), .in3(OutALU), .out(MuxA_Out), .sel(MuxASel));
  // Part2c_final_FunSel_main main_2: pin names not known; wires that end beside it: 2'b11, L_prime_H, Enable, main_2_p4[0], main_2_p4[1], main_2_p4[2], main_2_p4[3], main_2_p4[4], main_2_p4[5], main_2_p4[6], main_2_p4[7], IR_7_0[0], IR_7_0[1], IR_7_0[2], IR_7_0[3], IR_7_0[4], IR_7_0[5], IR_7_0[6], IR_7_0[7], DESTREG[0], DESTREG[1], DESTREG[2], IR_15_8[3], IR_15_8[4], IR_15_8[5], IR_15_8[6], IR_15_8[7]
  Multiplexer #(.width(8), .enable("false")) multiplexer_2 (.in0(OutC), .in1(OutA), .out(MUX_C_Out), .sel(MuxCSel));
  Multiplexer #(.select(2), .width(8), .enable("false")) multiplexer_3 (
    .in0({8{1'b0}}), .in1(IR_7_0), .in2(main_2_p4), .in3(OutALU), .out(MUX_B_Out), .sel(MuxBSel));
  Part1_main main_3 (
    .FunSel(FunSelALU), .A0(MUX_C_Out[0]), .A1(MUX_C_Out[1]), .A2(MUX_C_Out[2]), .A3(MUX_C_Out[3]),
    .A4(MUX_C_Out[4]), .A5(MUX_C_Out[5]), .A6(MUX_C_Out[6]), .A7(MUX_C_Out[7]), .B0(OutB[0]), .B1(OutB[1]),
    .B2(OutB[2]), .B3(OutB[3]), .B4(OutB[4]), .B5(OutB[5]), .B6(OutB[6]), .B7(OutB[7]), .ZERO(ZERO),
    .CARRY(CARRY), .NEGATIVE(NEGATIVE), .OVERFLOW(OVERFLOW), .OutALU0(OutALU[0]), .OutALU1(OutALU[1]),
    .OutALU2(OutALU[2]), .OutALU3(OutALU[3]), .OutALU4(OutALU[4]), .OutALU5(OutALU[5]), .OutALU6(OutALU[6]),
    .OutALU7(OutALU[7]));
  Part2b_final_main main_4 (
    .OutCSel(OutCSel), .OutDSel(OutDSel), .FunSel(FunSel), .RegSel(RegSel), .I0(MUX_B_Out[0]),
    .I1(MUX_B_Out[1]), .I2(MUX_B_Out[2]), .I3(MUX_B_Out[3]), .I4(MUX_B_Out[4]), .I5(MUX_B_Out[5]),
    .I6(MUX_B_Out[6]), .I7(MUX_B_Out[7]), .PC(PC), .AR(AR), .SP(SP), .OutC0(OutC[0]), .OutD0(OutD[0]),
    .OutC1(OutC[1]), .OutD1(OutD[1]), .OutC2(OutC[2]), .OutB2(OutD[2]), .OutC3(OutC[3]), .OutD3(OutD[3]),
    .OutC4(OutC[4]), .OutD4(OutD[4]), .OutC5(OutC[5]), .OutD5(OutD[5]), .OutC6(OutC[6]), .OutD6(OutD[6]),
    .OutC7(OutC[7]), .OutD7(OutD[7]));
  Clock u_CLK (.out(CLK_out));
  Multiplexer #(.width(8), .enable("false")) multiplexer_4 (
    .in0(D__load[7:0]), .in1(D__load[15:8]), .out(main_2_p4), .sel(MuxDSel));
  RAM #(.dataWidth(16), .bus("separate")) ram_1 (
    .addr(OutD), .din({{8{1'b0}}, OutALU}), .data(D__load), .str(Str), .sel(Sel), .clk(CLK_out), .ld(LD),
    .clr(CLR));
  Clock CLK_2 (.out(CLK_2_out));
  or or_1 (or_1_out, D4, D7, D8, D11, D12);
  D_Flip_Flop d_ff_2 (.clk(CLK_2_out), .D(or_1_out), .Q(S));  // open: Qn, preset, en, reset
  not not_1 (not_1_out, DESTREG[1]);
  not not_2 (not_2_out, IR_7_0[6]);
  not not_3 (not_3_out, IR_7_0[3]);
  and and_1 (and_1_out, DESTREG[0], not_1_out, DESTREG[2]);
  and and_2 (and_2_out, IR_7_0[5], not_2_out, IR_7_0[7]);
  and and_3 (and_3_out, IR_7_0[2], not_3_out, IR_7_0[4]);
  Multiplexer #(.width(3), .enable("false")) multiplexer_5 (
    .in0(IR_7_0[7:5]), .in1(3'b100), .out(SRCREG1_m), .sel(and_2_out));
  Multiplexer #(.width(3), .enable("false")) multiplexer_6 (
    .in0(IR_7_0[4:2]), .in1(3'b100), .out(SRCREG2_m), .sel(and_3_out));
  Comparator #(.width(3), .mode("unsigned")) comparator_1 (
    .a(SRCREG1_m), .b(SRCREG2_m), .eq(comparator_1_eq), .lt(comparator_1_lt));  // open: gt
  Multiplexer #(.width(3), .enable("false")) multiplexer_7 (
    .in0(DESTREG), .in1(3'b100), .out(multiplexer_7_out), .sel(and_1_out));
  Multiplexer #(.width(3), .enable("false")) multiplexer_8 (
    .in0(SRCREG2_m), .in1(SRCREG1_m), .out(multiplexer_8_out), .sel(comparator_1_lt));
  Multiplexer #(.width(3), .enable("false")) multiplexer_9 (
    .in0(SRCREG1_m), .in1(SRCREG2_m), .out(multiplexer_9_out), .sel(comparator_1_lt));
  not not_4 (not_4_out[0], A);
  not not_5 (not_5_out, ZERO);
  Multiplexer #(.select(2), .enable("false")) multiplexer_10 (
    .in0(1'b1), .in1(ZERO), .in2(not_5_out), .in3(S), .out(multiplexer_10_out[0]), .sel(CD));
  assign out_51 = D0 ? {IR_15_8[7:3], 1'b0, DESTREG[2:1], 3'b000, A, not_4_out[0]} : 13'bz;  // Controlled_Buffer controlled_buffer_1
  assign out_51 = D1 ? {IR_15_8[7:3], 1'b0, DESTREG[2:1], {5{1'b0}}} : 13'bz;  // Controlled_Buffer controlled_buffer_2
  assign out_51 = D2 ? {IR_15_8[7:3], multiplexer_7_out, SRCREG1_m, 2'b00} : 13'bz;  // Controlled_Buffer controlled_buffer_3
  assign out_51 = D3 ? {IR_15_8[7:3], multiplexer_7_out, {5{1'b0}}} : 13'bz;  // Controlled_Buffer controlled_buffer_4
  assign out_51 = D4 ? {IR_15_8[7:3], multiplexer_7_out, {5{1'b0}}} : 13'bz;  // Controlled_Buffer controlled_buffer_5
  assign out_51 = D5 ? {IR_15_8[7:3], multiplexer_7_out, multiplexer_8_out[1:0], multiplexer_9_out} : 13'bz;  // Controlled_Buffer controlled_buffer_6
  assign out_51 = D6 ? {IR_15_8[7:3], multiplexer_7_out, SRCREG1_m, SRCREG2_m[1:0]} : 13'bz;  // Controlled_Buffer controlled_buffer_7
  assign out_51 = D7 ? {IR_15_8[7:3], multiplexer_7_out, SRCREG1_m, 2'b00} : 13'bz;  // Controlled_Buffer controlled_buffer_8
  assign out_51 = D8 ? {IR_15_8[7:3], multiplexer_7_out, SRCREG1_m, 2'b00} : 13'bz;  // Controlled_Buffer controlled_buffer_9
  assign out_51 = D9 ? {IR_15_8[7:3], multiplexer_7_out, multiplexer_8_out[1:0], multiplexer_9_out} : 13'bz;  // Controlled_Buffer controlled_buffer_10
  assign out_51 = D10 ? {IR_15_8[7:3], multiplexer_7_out, multiplexer_8_out[1:0], multiplexer_9_out} : 13'bz;  // Controlled_Buffer controlled_buffer_11
  assign out_51 = D11 ? {IR_15_8[7:3], multiplexer_7_out, SRCREG1_m, 2'b00} : 13'bz;  // Controlled_Buffer controlled_buffer_12
  assign out_51 = D12 ? {IR_15_8[7:3], multiplexer_7_out, SRCREG1_m, 2'b00} : 13'bz;  // Controlled_Buffer controlled_buffer_13
  assign out_51 = D13 ? {IR_15_8[7:3], multiplexer_7_out, SRCREG1_m, 2'b00} : 13'bz;  // Controlled_Buffer controlled_buffer_14
  assign out_51 = D14 ? {IR_15_8[7:3], {8{1'b0}}} : 13'bz;  // Controlled_Buffer controlled_buffer_15
  assign out_51 = D15 ? {IR_15_8[7:3], {8{1'b0}}} : 13'bz;  // Controlled_Buffer controlled_buffer_16
  assign out_51 = D16 ? {IR_15_8[7:3], {8{1'b0}}} : 13'bz;  // Controlled_Buffer controlled_buffer_17
  assign out_51 = D17 ? {IR_15_8[7:3], {8{1'b0}}} : 13'bz;  // Controlled_Buffer controlled_buffer_18
  assign out_51 = D18 ? {IR_15_8[7:3], {8{1'b0}}} : 13'bz;  // Controlled_Buffer controlled_buffer_19
  Multiplexer #(.select(2), .width(2), .enable("false")) multiplexer_11 (
    .in0({1'b0, multiplexer_10_out[0]}), .in1({1'b0, multiplexer_10_out[0]}), .in2(BR), .in3(BR),
    .out(out_52), .sel(BR));
  Clock clock_1 (.out(clock_1_out));
  Clock CLK_3 (.out(CLK));
  Register #(.width(13)) CAR (.D(out_53), .Q(CAR_q), .clk(clock_1_out));  // open: en, clr
  Decoder #(.select(5), .enable("false")) decoder_1 (
    .out0(D0), .out1(D1), .out2(D2), .out3(D3), .out4(D4), .out5(D5), .out6(D6), .out7(D7), .out8(D8),
    .out9(D9), .out10(D10), .out11(D11), .out12(D12), .out13(D13), .out14(D14), .out15(D15), .out16(D16),
    .out17(D17), .out18(D18), .sel(IR_15_8[7:3]));  // open: out19, out20, out21, out22, out23, out24, out25, out26, out27, out28, out29, out30, out31
  Multiplexer #(.select(2), .width(13), .enable("false")) multiplexer_12 (
    .in0(out_55), .in1(out_56[12:0]), .in2(out_54), .in3(out_51), .out(out_53), .sel(out_52));
  ROM #(.addrWidth(13), .dataWidth(31)) rom_1 (
    .addr(CAR_q), .data({F1, F2, F3, F4, CD, BR, out_56[12:0]}));  // open: sel
  Adder #(.width(13)) adder_1 (.a(13'h1), .b(CAR_q), .out(out_55));  // open: cin, cout
  Register #(.width(13)) register_1 (.D(out_55), .Q(out_54), .clk(clock_1_out));  // open: en, clr
  not not_6 (not_6_out, F2[2]);
  not not_7 (not_7_out, F3[2]);
  not not_8 (not_8_out, F2[2]);
  not not_9 (not_9_out, F2[2]);
  and and_4 (and_4_out, not_6_out, not_7_out, O2);
  or or_2 (or_2_out, O5, O6, O9, O10, O11, O12, O13);
  and and_5 (and_5_out, A, O0);
  and and_6 (and_6_out, not_9_out, O4);
  not not_10 (not_10_out, F2[2]);
  and and_7 (and_7_out, not_8_out, or_2_out);
  not not_11 (not_11_out, F4[2]);
  or or_3 (or_3_out, O5, O9, O10);
  not not_12 (not_12_out, F3[2]);
  or or_4 (or_4_out, O6, O12, O13);
  or or_5 (or_5_out, and_5_out, and_6_out);
  and and_8 (and_8_out, not_10_out, F3[2], O2);
  not not_13 (not_13_out, F3[2]);
  not not_14 (not_14_out, F2[2]);
  not not_15 (not_15_out, F3[2]);
  or or_6 (or_6_out, and_4_out, and_7_out);
  Decoder #(.select(3), .enable("false")) decoder_2 (
    .out0(F2_0), .out1(F2_1), .out2(F2_2), .out3(F2_3), .out4(F2_4), .out5(F2_5), .out6(F2_6), .out7(F2_7),
    .sel(F2));
  Decoder #(.select(3), .enable("false")) decoder_3 (
    .out0(F4_0), .out1(F4_1), .out2(F4_2), .out3(F4_3), .out4(F4_4), .out5(F4_5), .out6(F4_6), .out7(F4_7),
    .sel(F4));
  not not_16 (not_16_out, F2[2]);
  or or_7 (or_7_out, O2, O4, O5, O6, O7, O8, O9, O10, O11, O12, O13);
  and and_9 (and_9_out, not_13_out, O2);
  and and_10 (and_10_out, not_14_out, O3);
  assign FunSelALU = O5 ? 4'b0100 : 4'bz;  // Controlled_Buffer controlled_buffer_20
  assign FunSelALU = O6 ? 4'b0110 : 4'bz;  // Controlled_Buffer controlled_buffer_21
  assign FunSelALU = O9 ? 4'b0111 : 4'bz;  // Controlled_Buffer controlled_buffer_22
  assign FunSelALU = O10 ? 4'b1000 : 4'bz;  // Controlled_Buffer controlled_buffer_23
  and and_11 (and_11_out, not_15_out, O11);
  and and_12 (and_12_out, F3[2], O11);
  assign FunSelALU = O12 ? 4'b1010 : 4'bz;  // Controlled_Buffer controlled_buffer_24
  assign FunSelALU = O13 ? 4'b1011 : 4'bz;  // Controlled_Buffer controlled_buffer_25
  assign MuxASel = or_5_out ? 2'b01 : 2'bz;  // Controlled_Buffer controlled_buffer_26
  assign MuxASel = and_8_out ? 2'b10 : 2'bz;  // Controlled_Buffer controlled_buffer_27
  assign MuxASel = or_6_out ? 2'b11 : 2'bz;  // Controlled_Buffer controlled_buffer_28
  and and_13 (and_13_out, not_16_out, or_7_out);
  and and_14 (and_14_out, not_11_out, or_3_out);
  and and_15 (and_15_out, not_12_out, or_4_out);
  or or_8 (or_8_out, O1, and_9_out, and_10_out);
  assign FunSelALU = and_11_out ? 4'b0011 : 4'bz;  // Controlled_Buffer controlled_buffer_29
  assign FunSelALU = and_12_out ? 4'b0010 : 4'bz;  // Controlled_Buffer controlled_buffer_30
  Decoder #(.select(5), .enable("false")) decoder_4 (
    .out0(O0), .out1(O1), .out2(O2), .out3(O3), .out4(O4), .out5(O5), .out6(O6), .out7(O7), .out8(O8),
    .out9(O9), .out10(O10), .out11(O11), .out12(O12), .out13(O13), .out14(O14), .out15(O15), .out16(O16),
    .out17(O17), .out18(O18), .out19(O19), .sel(F1));  // open: out20, out21, out22, out23, out24, out25, out26, out27, out28, out29, out30, out31
  or or_9 (or_9_out, and_14_out, and_15_out);
  assign FunSelALU = or_8_out ? 4'b0001 : 4'bz;  // Controlled_Buffer controlled_buffer_31
  or or_10 (or_10_out, O0, and_13_out);
  nor nor_1 (nor_1_out, or_5_out, and_8_out, or_6_out);
  assign RegSelRegister = or_10_out ? {F2_3, F2_2, F2_1, F2_0} : 4'bz;  // Controlled_Buffer controlled_buffer_32
  assign OutASel = or_9_out ? F3[1:0] : 2'bz;  // Controlled_Buffer controlled_buffer_33
  not not_17 (not_17_out, or_9_out);
  assign MuxASel = nor_1_out ? 2'b00 : 2'bz;  // Controlled_Buffer controlled_buffer_34
  not not_18 (not_18_out, or_10_out);
  nor nor_2 (nor_2_out, or_8_out, O5, O6, O9, O10, and_11_out, and_12_out, O12, O13);
  Decoder #(.select(3), .enable("false")) decoder_5 (
    .out0(F3_0), .out1(F3_1), .out2(F3_2), .out3(F3_3), .out4(F3_4), .out5(F3_5), .out6(F3_6), .out7(F3_7),
    .sel(F3));
  assign OutASel = not_17_out ? 2'b00 : 2'bz;  // Controlled_Buffer controlled_buffer_35
  assign FunSelALU = nor_2_out ? 4'b0000 : 4'bz;  // Controlled_Buffer controlled_buffer_36
  assign RegSelRegister = not_18_out ? 4'b0000 : 4'bz;  // Controlled_Buffer controlled_buffer_37
  not not_19 (not_19_out, F2[2]);
  not not_20 (not_20_out, F3[2]);
  or or_11 (or_11_out, O2, O11);
  not not_21 (not_21_out, F4[2]);
  assign RegSel = O14 ? 3'b001 : 3'bz;  // Controlled_Buffer controlled_buffer_38
  not not_22 (not_22_out, F2[2]);
  and and_16 (and_16_out, not_19_out, O3);
  or or_12 (or_12_out, O5, O9, O10);
  or or_13 (or_13_out, O2, O4, O5, O6, O7, O8, O9, O10, O11, O12, O13);
  or or_14 (or_14_out, O2, O4, O5, O6, O9, O10, O11, O12, O13);
  and and_17 (and_17_out, not_20_out, or_11_out);
  and and_18 (and_18_out, F4[2], or_12_out);
  and and_19 (and_19_out, not_21_out, or_12_out);
  and and_20 (and_20_out, F2[2], or_13_out);
  or or_15 (or_15_out, O2, O5, O6, O9, O10, O11, O12, O13);
  assign MuxBSel = and_21_out ? 2'b10 : 2'bz;  // Controlled_Buffer controlled_buffer_39
  and and_21 (and_21_out, F2[2], O4);
  assign MuxBSel = O14 ? 2'b01 : 2'bz;  // Controlled_Buffer controlled_buffer_40
  and and_22 (and_22_out, not_22_out, or_14_out);
  and and_23 (and_23_out, not_22_out, O7);
  and and_24 (and_24_out, not_22_out, O8);
  or or_16 (or_16_out, O1, and_16_out);
  assign RegSel = and_20_out ? {F2_7, F2_6, F2_4} : 3'bz;  // Controlled_Buffer controlled_buffer_41
  nor nor_3 (nor_3_out, and_20_out, O14);
  and and_25 (and_25_out, F2[2], or_15_out);
  or or_17 (or_17_out, O0, and_22_out);
  assign out_50 = or_16_out ? F2[1:0] : 2'bz;  // Controlled_Buffer controlled_buffer_42
  assign out_50 = or_18_out ? F3[1:0] : 2'bz;  // Controlled_Buffer controlled_buffer_43
  or or_18 (or_18_out, and_17_out, and_18_out);
  assign out_50 = or_19_out ? F4[1:0] : 2'bz;  // Controlled_Buffer controlled_buffer_44
  or or_19 (or_19_out, and_19_out, O6);
  assign RegSel = nor_3_out ? 3'b000 : 3'bz;  // Controlled_Buffer controlled_buffer_45
  assign MuxBSel = and_25_out ? 2'b11 : 2'bz;  // Controlled_Buffer controlled_buffer_46
  assign FunSelRegister = or_17_out ? 2'b01 : 2'bz;  // Controlled_Buffer controlled_buffer_47
  assign FunSelRegister = and_23_out ? 2'b11 : 2'bz;  // Controlled_Buffer controlled_buffer_48
  assign FunSelRegister = and_24_out ? 2'b10 : 2'bz;  // Controlled_Buffer controlled_buffer_49
  nor nor_4 (nor_4_out, or_17_out, and_23_out, and_24_out);
  assign MuxBSel = nor_5_out ? 2'b00 : 2'bz;  // Controlled_Buffer controlled_buffer_50
  nor nor_5 (nor_5_out, and_25_out, and_21_out, O14);
  assign FunSelRegister = nor_4_out ? 2'b00 : 2'bz;  // Controlled_Buffer controlled_buffer_51
  nor nor_6 (nor_6_out, or_16_out, or_18_out, or_19_out);
  assign out_50 = nor_6_out ? 2'b00 : 2'bz;  // Controlled_Buffer controlled_buffer_52
  and and_26 (and_26_out, F2[2], O3);
  or or_20 (or_20_out, O5, O9, O10);
  or or_21 (or_21_out, O2, O4, O5, O6, O9, O10, O11, O12, O13);
  and and_27 (and_27_out, F2[2], F3[2], O2);
  or or_22 (or_22_out, O6, O11, O12, O13);
  and and_28 (and_28_out, F4[2], or_20_out);
  and and_29 (and_29_out, F3[2], or_22_out);
  and and_30 (and_30_out, F2[2], or_21_out);
  or or_23 (or_23_out, O2, O6, O11, O12, O13);
  or or_24 (or_24_out, O5, O9, O10);
  or or_25 (or_25_out, and_30_out, O14);
  and and_31 (and_31_out, F2[2], O7);
  and and_32 (and_32_out, F2[2], O8);
  assign OutCSel = and_33_out ? {F2_7, F2_6} : 2'bz;  // Controlled_Buffer controlled_buffer_53
  and and_33 (and_33_out, F2[2], O3);
  and and_34 (and_34_out, F4[2], or_24_out);
  assign OutCSel = O19 ? 2'b00 : 2'bz;  // Controlled_Buffer controlled_buffer_54
  assign FunSel = or_25_out ? 2'b01 : 2'bz;  // Controlled_Buffer controlled_buffer_55
  assign FunSel = and_31_out ? 2'b11 : 2'bz;  // Controlled_Buffer controlled_buffer_56
  assign FunSel = and_32_out ? 2'b10 : 2'bz;  // Controlled_Buffer controlled_buffer_57
  or or_26 (or_26_out, and_27_out, and_26_out, and_28_out, and_29_out);
  and and_35 (and_35_out, F3[2], or_23_out);
  assign OutCSel = and_34_out ? {F4_7, F4_6} : 2'bz;  // Controlled_Buffer controlled_buffer_58
  assign MuxCSel = or_26_out ? 1'b0 : 1'bz;  // Controlled_Buffer controlled_buffer_59
  assign OutCSel = and_35_out ? {F3_7, F3_6} : 2'bz;  // Controlled_Buffer controlled_buffer_60
  assign FunSel = nor_7_out ? 2'b00 : 2'bz;  // Controlled_Buffer controlled_buffer_61
  nor nor_7 (nor_7_out, or_25_out, and_31_out, and_32_out);
  assign MuxCSel = not_23_out ? 1'b1 : 1'bz;  // Controlled_Buffer controlled_buffer_62
  not not_23 (not_23_out, or_26_out);
  nor nor_8 (nor_8_out, and_35_out, and_34_out, O19);
  assign OutCSel = nor_8_out ? 2'b00 : 2'bz;  // Controlled_Buffer controlled_buffer_63
  not not_24 (not_24_out, F4[0]);
  not not_25 (not_25_out, F4[0]);
  and and_36 (and_36_out, A, O0);
  or or_27 (or_27_out, O1, O3, O4, O19);
  and and_37 (and_37_out, A, O0);
  or or_28 (or_28_out, O4, O19);
  and and_38 (and_38_out, not_24_out, O19);
  and and_39 (and_39_out, O19, F2_0, F3_0);
  and and_40 (and_40_out, not_25_out, O19);
  and and_41 (and_41_out, A, O0);
  or or_29 (or_29_out, and_37_out, or_28_out);
  or or_30 (or_30_out, O1, O3);
  assign MuxDSel = and_38_out ? 1'b1 : 1'bz;  // Controlled_Buffer controlled_buffer_64
  assign Enable = and_39_out ? 1'b1 : 1'bz;  // Controlled_Buffer controlled_buffer_65
  assign L_prime_H = and_40_out ? 1'b1 : 1'bz;  // Controlled_Buffer controlled_buffer_66
  or or_31 (or_31_out, and_41_out, O1);
  assign OutDSel = or_32_out ? 2'b10 : 2'bz;  // Controlled_Buffer controlled_buffer_67
  or or_32 (or_32_out, O3, O4);
  assign Sel = or_33_out ? 1'b1 : 1'bz;  // Controlled_Buffer controlled_buffer_68
  or or_33 (or_33_out, and_36_out, or_27_out);
  assign LD = or_29_out ? 1'b1 : 1'bz;  // Controlled_Buffer controlled_buffer_69
  assign Str = or_30_out ? 1'b1 : 1'bz;  // Controlled_Buffer controlled_buffer_70
  not not_26 (not_26_out, and_38_out);
  not not_27 (not_27_out, and_39_out);
  not not_28 (not_28_out, and_40_out);
  assign OutDSel = or_31_out ? 2'b01 : 2'bz;  // Controlled_Buffer controlled_buffer_71
  not not_29 (not_29_out, or_33_out);
  not not_30 (not_30_out, or_29_out);
  assign Str = not_31_out ? 1'b0 : 1'bz;  // Controlled_Buffer controlled_buffer_72
  not not_31 (not_31_out, or_30_out);
  assign MuxDSel = not_26_out ? 1'b0 : 1'bz;  // Controlled_Buffer controlled_buffer_73
  assign Enable = not_27_out ? 1'b0 : 1'bz;  // Controlled_Buffer controlled_buffer_74
  assign L_prime_H = not_28_out ? 1'b0 : 1'bz;  // Controlled_Buffer controlled_buffer_75
  assign Sel = not_29_out ? 1'b0 : 1'bz;  // Controlled_Buffer controlled_buffer_76
  assign LD = not_30_out ? 1'b0 : 1'bz;  // Controlled_Buffer controlled_buffer_77
  nor nor_9 (nor_9_out, or_31_out, or_32_out);
  assign OutDSel = nor_9_out ? 2'b00 : 2'bz;  // Controlled_Buffer controlled_buffer_78

  assign FunSelAddress = FunSel;
  assign FunSelALU_2 = FunSelALU;
  assign FunSelRegister_2 = FunSelRegister;
  assign IR_7_0_2 = IR_7_0;
  assign IR_15_8[2:0] = DESTREG;
  assign IR_15_8_2 = {IR_15_8[7:3], DESTREG};
  assign MuxASel_2 = MuxASel;
  assign MuxBSel_2 = MuxBSel;
  assign Opcode = IR_15_8[7:3];
  assign Opcode_2 = IR_15_8[7:3];
  assign Opcode_3 = IR_15_8[7:3];
  assign out_16 = F1;
  assign out_21 = F2;
  assign out_22 = F3;
  assign out_32 = F4;
  assign out_45 = MuxDSel;
  assign out_48 = IR_7_0[7:5];
  assign out_49 = IR_7_0[4:2];
  assign out_56[30:13] = {F1, F2, F3, F4, CD, BR};
  assign out_77 = D__load;
  assign OutASel_2 = OutASel;
  assign OutASel_3 = out_50;
  assign OutBSel = out_50;
  assign OutCSel_2 = OutCSel;
  assign OutDSel_2 = OutDSel;
  assign RegSel_2 = DESTREG[2:1];
  assign RegSelAddress = RegSel;
  assign RegSelRegister_2 = RegSelRegister;
  assign Rx = DESTREG[2:1];
  assign SRCREG1 = IR_7_0[7:5];
  assign SRCREG2 = IR_7_0[4:2];

  // Other names for the same wires on the sheet: DR1 = DESTREG[1]; DR2 = DESTREG[2]; DR0 = DESTREG[0];
  //   MAP[12:0] = out_51; S1R0 = IR_7_0[5]; S1R1 = IR_7_0[6]; S1R2 = IR_7_0[7]; F4_2LSB[1:0] = F4[1:0];
  //   F4_LSB = F4[0]; F4_MSB = F4[2]; F3_2LSB[1:0] = F3[1:0]; F3_MSB = F3[2]; F2_2LSB[1:0] = F2[1:0]; F2_MSB = F2[2];
  //   S2R0 = IR_7_0[2]; S2R1 = IR_7_0[3]; S2R2 = IR_7_0[4]; Z = ZERO

  // Notes on the sheet:
  //   RegSelAddress
  //   Register File
  //   MUX A
  //   IR
  //   MUX C
  //   MUX B
  //   Address Register File
  //   MUX D
  //   CD
  //   BR
  //   contents of rom_1 (hex, n*v repeats v):
  //   2da1300 1300 1300 30*0 801300 801300 30*0 1001300 1001300 30*0 1801300 1801300 157*0 4001300 31*0
  //   4801300 31*0 5001300 31*0 5801300 159*0 8001300 8005300 0 0 8101300 8105300 0 0 8201300 8205300 0 0
  //   8301300 8305300 0 0 8401300 8405300 6*0 8601300 8605300 0 0 8701300 8705300 0 0 8801300 8805300 0 0
  //   8901300 8905300 0 0 8a01300 8a05300 0 0 8b01300 8b05300 0 0 8c01300 8c05300 6*0 8e01300 8e05300 0 0
  //   8f01300 8f05300 0 0 9001300 9005300 0 0 9101300 9105300 0 0 9201300 9205300 0 0 9301300 9305300 0 0
  //   9401300 9405300 6*0 9601300 9605300 0 0 9701300 9705300 0 0 9801300 9805300 0 0 9901300 9905300 0 0
  //   9a01300 9a05300 0 0 9b01300 9b05300 0 0 9c01300 9c05300 6*0 9e01300 9e05300 0 0 9f01300 9f05300 0 0
  //   a001300 a005300 0 0 a101300 a105300 0 0 a201300 a205300 0 0 a301300 a305300 0 0 a401300 a405300 6*0
  //   a601300 a605300 0 0 a701300 a705300 34*0 b001300 b005300 0 0 b101300 b105300 0 0 b201300 b205300 0 0
  //   b301300 b305300 0 0 b401300 b405300 6*0 b601300 b605300 0 0 b701300 b705300 0 0 b801300 b805300 0 0
  //   b901300 b905300 0 0 ba01300 ba05300 0 0 bb01300 bb05300 0 0 bc01300 bc05300 6*0 be01300 be05300 0 0
  //   bf01300 bf05300 0 0 c0007e1 31*0 c8007e1 31*0 d0007e1 31*0 d8007e1 31*0 e0007e1 eda07e1 62*0 f0007e1
  //   31*0 f8007e1 31*0 12da28e1 10001300 30*0 12da28e1 10801300 30*0 12da28e1 11001300 30*0 12da28e1
  //   11801300 30*0 12da28e1 12001300 62*0 12da28e1 13001300 30*0 12da28e1 13801300 30*0 14001300 14021300
  //   14041300 14061300 14081300 0 140c1300 140e1300 0 14121300 14141300 14161300 14181300 0 141c1300
  //   141e1300 0 0 14241300 14261300 14281300 0 142c1300 142e1300 0 0 0 14361300 14381300 0 143c1300
  //   143e1300 14801300 14821300 14841300 14861300 14881300 0 148c1300 148e1300 0 14921300 14941300
  //   14961300 14981300 0 149c1300 149e1300 0 0 14a41300 14a61300 14a81300 0 14ac1300 14ae1300 0 0 0
  //   14b61300 14b81300 0 14bc1300 14be1300 15001300 15021300 15041300 15061300 15081300 0 150c1300
  //   150e1300 0 15211300 15141300 15161300 15181300 0 151c1300 151e1300 0 0 15241300 15261300 15281300 0
  //   152c1300 152e1300 0 0 0 15361300 15381300 0 153c1300 153e1300 15801300 15821300 15841300 15861300
  //   15881300 0 158c1300 158e1300 0 15921399 15941300 15961300 15981300 0 159c1300 159e1300 0 0 15a41300
  //   15a61300 15a81300 0 15ac1300 15ae1300 0 0 0 15b61300 15b81300 0 15bc1300 15be1300 16001300 16021300
  //   16041300 16061300 16081300 0 160c1300 160e1300 0 16121300 16141300 16161300 16181300 0 161c1300
  //   161e1300 0 0 16241300 16261300 16281300 0 162c1300 162e1300 0 0 0 16361300 16381300 0 163c1300
  //   163e1300 32*0 17001300 17021300 17041300 17061300 17081300 0 170c1300 170e1300 0 17121300 17141300
  //   17161300 17181300 0 171c1300 171e1300 0 0 17241300 17261300 17281300 0 172c1300 172e1300 0 0 0
  //   17361300 17381300 0 173c1300 173e1300 17801300 17821300 17841300 17861300 17881300 0 178c1300
  //   178e1300 0 17921300 17941300 17961300 17981300 0 179c1300 179e1300 0 0 17a41300 17a61300 17a81300 0
  //   17ac1300 17ae1300 0 0 0 17b61300 17b81300 0 17bc1300 17be1300 18001300 18021300 18041300 18061300
  //   18101300 18121300 18141300 18161300 18201300 18221300 18241300 18261300 18301300 18321300 18341300
  //   18361300 18401300 18421300 18441300 18461300 4*0 18601300 18621300 18641300 18661300 18701300
  //   18721300 18741300 18761300 18801300 18821300 18841300 18861300 18901300 18921300 18941300 18961300
  //   18a01300 18a21300 18a41300 18a61300 18b01300 18b21300 18b41300 18b61300 18c01300 18c21300 18c41300
  //   18c61300 4*0 18e01300 18e21300 18e41300 18e61300 18f01300 18f21300 18f41300 18f61300 19001300
  //   19021300 19041300 19061300 19101300 19121300 19141300 19161300 19201300 19221300 19241300 19261300
  //   19301300 19321300 19341300 19361300 19401300 19421300 19441300 19461300 4*0 19601300 19621300
  //   19641300 19661300 19701300 19721300 19741300 19761300 19801300 19821300 19841300 19861300 19901300
  //   19921300 19941300 19961300 19a01300 19a21300 19a41300 19a61300 19b01300 19b21300 19b41300 19b61300
  //   19c01300 19c21300 19c41300 19c61300 4*0 19e01300 19e21300 19e41300 19e61300 19f01300 19f21300
  //   19f41300 19f61300 1a001300 1a021300 1a041300 1a061300 1a101300 1a121300 1a141300 1a1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
  //   Next Address
  //   MuxASel
  //   RegSelRegister
  //   OutASel
  //   FunSelALU
  //   OutBSel
  //   RegSelAddress
  //   MuxBSel
  //   FunSelRegister
  //   MuxCSel
  //   OutCSel
  //   L'/H
  //   MuxDSel
  //   Enable IR
  //   Sel
  //   LD
  //   Str
  //   OutDSel
endmodule
