// Logisim project overflow.circ as structural Verilog: 1 circuit, main circuit main
module main (
  input  MuxCSel,
  input  [3:0] FunSel,
  input  [3:0] RegSel,
  input  [1:0] FunSel_2,
  input  [1:0] OutBSel,
  input  [1:0] OutASel,
  input  CLR,
  input  [1:0] MuxASel,
  input  Str,
  input  Sel,
  input  [2:0] RegSel_2,
  input  LD,
  input  [1:0] FunSel_3,
  input  [1:0] OutDSel,
  input  [1:0] OutCSel,
  input  E,
  input  L_prime_H,
  input  [1:0] FunSel_4,
  input  [1:0] MuxBSel,
  output [7:0] OutB,
  output ZERO,
  output CARRY,
  output NEGATIVE,
  output OVERFLOW,
  output [7:0] OutA,
  output [7:0] MUX_C_Out,
  output [7:0] OutALU,
  output [7:0] D__load,
  output [7:0] MuxA_Out,
  output [7:0] OutC,
  output [7:0] IR_0_7,
  output [7:0] OutD,
  output [7:0] IR_8_15,
  output [7:0] MUX_B_Out
);

  wire CLK_out;

  // Part2a_final_main main_1: pin names not known; wires that end beside it: OutASel, OutBSel, FunSel_2, RegSel, MuxA_Out[0], MuxA_Out[1], MuxA_Out[2], MuxA_Out[3], MuxA_Out[4], MuxA_Out[5], MuxA_Out[6], MuxA_Out[7], OutA[0], OutB[0], OutA[1], OutB[1], OutA[2], OutB[2], OutA[3], OutB[3], OutA[4], OutB[4], OutA[5], OutB[5], OutA[6], OutB[6], OutA[7], OutB[7]
  Multiplexer #(.select(2), .width(8), .enable("false")) multiplexer_1 (
    .in0(IR_0_7), .in1(D__load), .in2(OutC), .in3(OutALU), .out(MuxA_Out), .sel(MuxASel));
  // Part2c_final_FunSel_main main_2: pin names not known; wires that end beside it: FunSel_4, L_prime_H, E, D__load[0], D__load[1], D__load[2], D__load[3], D__load[4], D__load[5], D__load[6], D__load[7], IR_0_7[0], IR_0_7[1], IR_0_7[2], IR_0_7[3], IR_0_7[4], IR_0_7[5], IR_0_7[6], IR_0_7[7], IR_8_15[0], IR_8_15[1], IR_8_15[2], IR_8_15[3], IR_8_15[4], IR_8_15[5], IR_8_15[6], IR_8_15[7]
  Multiplexer #(.width(8), .enable("false")) multiplexer_2 (.in0(MuxA_Out), .in1(OutA), .out(MUX_C_Out), .sel(MuxCSel));
  Multiplexer #(.select(2), .width(8), .enable("false")) multiplexer_3 (
    .in0({8{1'b0}}), .in1(IR_0_7), .in2(D__load), .in3(OutALU), .out(MUX_B_Out), .sel(MuxBSel));
  // Part1_zcno_main main_3: pin names not known; wires that end beside it: FunSel, MUX_C_Out[0], MUX_C_Out[1], MUX_C_Out[2], MUX_C_Out[3], MUX_C_Out[4], MUX_C_Out[5], MUX_C_Out[6], MUX_C_Out[7], OutB[0], OutB[1], OutB[2], OutB[3], OutB[4], OutB[5], OutB[6], OutB[7], ZERO, CARRY, NEGATIVE, OVERFLOW, OutALU[0], OutALU[1], OutALU[2], OutALU[3], OutALU[4], OutALU[5], OutALU[6], OutALU[7]
  // Part2b_final_main main_4: pin names not known; wires that end beside it: OutCSel, OutDSel, FunSel_3, RegSel_2, MUX_B_Out[0], MUX_B_Out[1], MUX_B_Out[2], MUX_B_Out[3], MUX_B_Out[4], MUX_B_Out[5], MUX_B_Out[6], MUX_B_Out[7], OutC[0], OutD[0], OutC[1], OutD[1], OutC[2], OutD[2], OutC[3], OutD[3], OutC[4], OutD[4], OutC[5], OutD[5], OutC[6], OutD[6], OutC[7], OutD[7]
  Clock CLK (.out(CLK_out));
  RAM #(.bus("separate")) ram_1 (
    .addr(OutD), .din(OutALU), .data(D__load), .str(Str), .sel(Sel), .clk(CLK_out), .ld(LD), .clr(CLR));

  // Notes on the sheet:
  //   Register File
  //   MUX A
  //   IR
  //   MUX C
  //   MUX B
  //   Address Register File
endmodule
